// Logisim project FPGA.circ as structural Verilog: 12 circuits, main circuit MotorController
module Pulser (
  input  Input,
  output Output
);


  assign Output = Input;
endmodule

// Pre.
module Prescaler (
  input  RST,
  input  CLK,
  output ScaledClock
);

  wire not_1_out;

  not not_1 (not_1_out, RST);
  and and_1 (ScaledClock, not_1_out, CLK);
endmodule

// Tim.
module Counter (
  input  RST,
  input  CLK,
  output [23:0] Output
);

  Counter_part #(.width(24), .max('hffffff)) counter_1 (
    .count(1'b1), .Q(Output), .clk(CLK), .clr(RST));  // open: load, D, carry
endmodule

// Enc.
module Encoder (
  input  Reset,
  input  Clock,
  input  [1:0] Input,
  output [7:0] Output
);
endmodule

// ENC\nCon.
module ENCController (
  input  RST,
  input  CLK,
  input  [1:0] ENCInput,
  output [23:0] ENCTime,
  output [7:0] ENCCount
);

  wire prescaler_1_scaledclock;

  Prescaler prescaler_1 (.RST(RST), .CLK(CLK), .ScaledClock(prescaler_1_scaledclock));
  Encoder encoder_1 (.Reset(RST), .Clock(CLK), .Output(ENCCount), .Input(ENCInput));
  Counter counter_1 (.RST(RST), .CLK(prescaler_1_scaledclock), .Output(ENCTime));
endmodule

module PWM (
  input  RST,
  input  CLK,
  input  [6:0] CompareMatch,
  output Output
);

  wire [6:0] counter_1_q;

  Counter_part #(.width(7), .max('h7f)) counter_1 (
    .count(1'b1), .Q(counter_1_q), .clk(CLK), .clr(RST));  // open: load, D, carry
  Comparator #(.width(7), .mode("unsigned")) comparator_1 (
    .a(counter_1_q), .b(CompareMatch), .lt(Output));  // open: gt, eq
endmodule

// PWM\nCon.
module PWMController (
  input  RST,
  input  CLK,
  input  [7:0] PWMCM,
  output [1:0] PWMOutput
);

  wire not_3_out, prescaler_1_scaledclock, pwm_1_output;
  wire [6:0] and_1_out, and_2_out, not_1_out, not_2_out, or_1_out;

  Prescaler prescaler_1 (.RST(RST), .CLK(CLK), .ScaledClock(prescaler_1_scaledclock));
  assign not_1_out = ~PWMCM[6:0];  // NOT_Gate not_1, 7 bits wide
  assign and_1_out = not_1_out & {7{PWMCM[7]}};  // AND_Gate and_1, 7 bits wide
  assign and_2_out = PWMCM[6:0] & not_2_out;  // AND_Gate and_2, 7 bits wide
  assign not_2_out = ~{7{PWMCM[7]}};  // NOT_Gate not_2, 7 bits wide
  PWM pwm_1 (.RST(RST), .CLK(prescaler_1_scaledclock), .CompareMatch(or_1_out), .Output(pwm_1_output));
  not not_3 (not_3_out, PWMCM[7]);
  assign or_1_out = and_1_out | and_2_out;  // OR_Gate or_1, 7 bits wide
  and and_3 (PWMOutput[0], not_3_out, pwm_1_output);
  and and_4 (PWMOutput[1], pwm_1_output, PWMCM[7]);
endmodule

module SIPO (
  input  RST,
  input  CLK,
  input  LATCH,
  input  SI,
  output [7:0] PO,
  output RW,
  output SO
);

  wire and_1_out, d_ff_2_q, d_ff_4_q, d_ff_6_q, d_ff_8_q, d_ff_10_q, d_ff_13_q, d_ff_14_q, d_ff_16_q,
       not_1_out;

  and and_1 (and_1_out, not_1_out, LATCH);
  not not_1 (not_1_out, SO);
  D_Flip_Flop d_ff_1 (.clk(and_1_out), .D(d_ff_2_q), .Q(PO[0]), .reset(RST));  // open: Qn, preset, en
  D_Flip_Flop d_ff_2 (.clk(CLK), .D(SI), .Q(d_ff_2_q), .reset(RST));  // open: Qn, preset, en
  D_Flip_Flop d_ff_3 (.clk(and_1_out), .D(d_ff_4_q), .Q(PO[1]), .reset(RST));  // open: Qn, preset, en
  D_Flip_Flop d_ff_4 (.clk(CLK), .D(d_ff_2_q), .Q(d_ff_4_q), .reset(RST));  // open: Qn, preset, en
  D_Flip_Flop d_ff_5 (.clk(and_1_out), .D(d_ff_6_q), .Q(PO[2]), .reset(RST));  // open: Qn, preset, en
  D_Flip_Flop d_ff_6 (.clk(CLK), .D(d_ff_4_q), .Q(d_ff_6_q), .reset(RST));  // open: Qn, preset, en
  D_Flip_Flop d_ff_7 (.clk(and_1_out), .D(d_ff_8_q), .Q(PO[3]), .reset(RST));  // open: Qn, preset, en
  D_Flip_Flop d_ff_8 (.clk(CLK), .D(d_ff_6_q), .Q(d_ff_8_q), .reset(RST));  // open: Qn, preset, en
  D_Flip_Flop d_ff_9 (.clk(and_1_out), .D(d_ff_10_q), .Q(PO[4]), .reset(RST));  // open: Qn, preset, en
  D_Flip_Flop d_ff_10 (.clk(CLK), .D(d_ff_8_q), .Q(d_ff_10_q), .reset(RST));  // open: Qn, preset, en
  D_Flip_Flop d_ff_11 (.clk(and_1_out), .D(d_ff_14_q), .Q(PO[6]), .reset(RST));  // open: Qn, preset, en
  D_Flip_Flop d_ff_12 (.clk(and_1_out), .D(d_ff_13_q), .Q(PO[5]), .reset(RST));  // open: Qn, preset, en
  D_Flip_Flop d_ff_13 (.clk(CLK), .D(d_ff_10_q), .Q(d_ff_13_q), .reset(RST));  // open: Qn, preset, en
  D_Flip_Flop d_ff_14 (.clk(CLK), .D(d_ff_13_q), .Q(d_ff_14_q), .reset(RST));  // open: Qn, preset, en
  D_Flip_Flop d_ff_15 (.clk(and_1_out), .D(d_ff_16_q), .Q(PO[7]), .reset(RST));  // open: Qn, preset, en
  D_Flip_Flop d_ff_16 (.clk(CLK), .D(d_ff_14_q), .Q(d_ff_16_q), .reset(RST));  // open: Qn, preset, en
  D_Flip_Flop d_ff_17 (.clk(LATCH), .D(SO), .Q(RW), .reset(RST));  // open: Qn, preset, en
  D_Flip_Flop d_ff_18 (.clk(CLK), .D(d_ff_16_q), .Q(SO), .reset(RST));  // open: Qn, preset, en
endmodule

module PISO (
  input  RST,
  input  CLK,
  input  LATCH,
  input  SI,
  output SO,
  output [31:0] PI
);
endmodule

// SPI\nCon.
module SPIController (
  input  RST,
  input  SPICLK,
  input  SPISS,
  input  SPIMOSI,
  input  [31:0] PI,
  output [7:0] PO,
  output SPIMSIO,
  output RW
);

  wire and_1_out, and_2_out, not_1_out, not_2_out, pulser_1_output, pulser_2_output;

  and and_1 (and_1_out, SPICLK, not_1_out);
  not not_1 (not_1_out, SPISS);
  Pulser pulser_1 (.Input(SPISS), .Output(pulser_1_output));
  not not_2 (not_2_out, RW);
  and and_2 (and_2_out, not_1_out, not_2_out);
  Pulser pulser_2 (.Input(and_2_out), .Output(pulser_2_output));
  SIPO sipo_1 (.RST(RST), .CLK(and_1_out), .LATCH(pulser_1_output), .SI(SPIMOSI), .PO(PO), .RW(RW));  // open: SO
  PISO piso_1 (.RST(RST), .CLK(and_1_out), .LATCH(pulser_2_output), .SO(SPIMSIO), .PI(PI));  // open: SI
endmodule

module MotorController (
  input  RST,
  input  CLK,
  input  SPICLK,
  input  SPISS,
  input  SPIMOSI,
  input  [1:0] ENCInput,
  output [1:0] PWMOutput,
  output SPIMISO,
  output RW
);

  wire [7:0] spicontroller_1_po;
  wire [31:0] enccontroller_1_enccount;

  SPIController spicontroller_1 (
    .RST(RST), .SPICLK(SPICLK), .SPISS(SPISS), .SPIMOSI(SPIMOSI), .SPIMSIO(SPIMISO), .PO(spicontroller_1_po),
    .PI(enccontroller_1_enccount), .RW(RW));
  PWMController pwmcontroller_1 (.RST(RST), .CLK(CLK), .PWMCM(spicontroller_1_po), .PWMOutput(PWMOutput));
  ENCController enccontroller_1 (
    .RST(CLK), .CLK(RST), .ENCTime(enccontroller_1_enccount[31:8]), .ENCCount(enccontroller_1_enccount[7:0]),
    .ENCInput(ENCInput));
endmodule

module FPGA (
  input  RST,
  input  CLK,
  input  SPI0CLK,
  input  SPI0SS,
  input  SPI0MOSI,
  input  [1:0] ENCInput0,
  input  SPI1CLK,
  input  SPI1SS,
  input  SPI1MOSI,
  input  [1:0] ENCInput1,
  input  SW_1,
  input  SW_0,
  input  SW_2,
  output [1:0] PWMOutput0,
  output PWMEN0,
  output SPI0MISO,
  output [1:0] PWMOutput1,
  output PWMEN1,
  output SPI1MISO
);

  nor nor_1 (PWMEN1, SW_1, SW_0);
  MotorController motorcontroller_1 (
    .RST(RST), .CLK(CLK), .SPICLK(SPI0CLK), .SPISS(SPI0SS), .SPIMOSI(SPI0MOSI), .SPIMISO(SPI0MISO),
    .PWMOutput(PWMOutput0), .ENCInput(ENCInput0));  // open: RW
  MotorController motorcontroller_2 (
    .RST(RST), .CLK(CLK), .SPICLK(SPI1CLK), .SPISS(SPI1SS), .SPIMOSI(SPI1MOSI), .SPIMISO(SPI1MISO),
    .PWMOutput(PWMOutput1), .ENCInput(ENCInput1));  // open: RW
  nor nor_2 (PWMEN0, SW_0, SW_2);
endmodule
